# Fritzing sketch RogerNav01 (saved by Fritzing 0.9.3b)

parts:
  Part1 = Arduino Mega 2560 (Rev3)  # not connected
  Part2 = Adafruit Feather M0 Basic Proto [part_number="Adafruit #2772"]
  Part3 = Adafruit FeatherWing Proto [part_number="Adafruit #2884"]
  Part4 = Adafruit FeatherWing Doubler [part_number="Adafruit #2890"]
  Part5 = Adafruit FXOS8700 + FXAS21002 9 DoF Breakout [part_number="Adafruit #3463"]  # not connected
  Part6 = Adafruit Bluefruit LE UART Friend [part_number="Adafruit #2479"]
  Part8 = Adafruit Adalogger FeatherWing [part_number="Adafruit #2922"]
  Part9 = Adafruit GPS FeatherWing [part_number="Adafruit #3133"]
  Part10 = Arduino Mega Proto Shield (v6)
  R1 = Resistor [tolerance=±5% resistance=10k package=THT]  # not connected

nets (from the schematic view):
  GND: Part2.GND, Part3.G, Part3.GND, Part4.G, Part4.GND
  N1: Part2.D1, Part3.TX, Part4.TX
  N2: Part2.D0, Part3.RX, Part4.RX
  N3: Part2.MISO, Part3.MISO, Part4.MISO
  N4: Part2.MOSI, Part3.MOSI, Part4.MOSI
  N5: Part2.SCK, Part3.SCK, Part4.SCK
  N6: Part2.A5, Part3.F, Part4.F
  N7: Part2.A4, Part3.E, Part4.E
  N8: Part2.A3, Part3.D, Part4.D
  N9: Part2.A2, Part3.C, Part4.C
  N10: Part2.A1, Part3.B, Part4.B
  N11: Part2.A0, Part3.A, Part4.A
  N12: Part2.AREF, Part3.AREF, Part4.AREF
  N13: Part2.+3V3, Part3.3V, Part4.3V
  N14: Part2.!RESET, Part3.RST, Part4.RESET
  N15: Part2.VBAT, Part3.VBAT, Part4.VBAT
  N16: Part2.EN, Part3.EN, Part4.EN
  N17: Part2.VBUS, Part3.USB, Part4.USB
  N18: Part2.D13, Part3.N, Part4.O
  N19: Part2.D12, Part3.M, Part4.N
  N20: Part2.D11, Part3.L, Part4.M
  N21: Part2.D10, Part3.K, Part4.L
  N22: Part2.D9, Part3.J, Part4.K
  N23: Part2.D6, Part3.I, Part4.J
  N24: Part2.D5, Part3.H, Part4.I
  N25: Part2.SCL, Part3.SCL, Part4.SCL
  N26: Part2.SDA, Part3.SDA, Part4.SDA
  N27: Part6.DFU, Part10.N$168
  N28: Part6.GND, Part10.N$156
  N29: Part6.RTS, Part10.N$135
  N30: Part6.VIN, Part10.N$132
  N31: Part6.RXI, Part10.N$120
  N32: Part6.TXO, Part10.N$107
  N33: Part6.CTS, Part10.N$95
  N34: Part6.MODE, Part10.N$83
  N35: Part8.USB, Part9.USB, Part10.N$403
  N36: Part8.N, Part9.N, Part10.N$401
  N37: Part8.L, Part9.L, Part10.N$197
  N38: Part8.F, Part9.F, Part10.N$441
  N39: Part8.D, Part9.D, Part10.N$324
  N40: Part8.C, Part9.C, Part10.N$368
  N41: Part8.B, Part9.B, Part10.N$369
  N42: Part8.A, Part9.A, Part10.N$370
  GND_2: Part8.GND, Part9.GND, Part10.N$371
  N43: Part8.RESET, Part9.RST, Part10.N$374
  N44: Part8.+3V3, Part9.3V, Part10.N$373
  N45: Part8.AREF, Part9.AREF, Part10.N$372
  N46: Part8.SCK, Part9.SCK, Part10.N$442
  N47: Part8.MOSI, Part9.MOSI, Part10.N$443
  N48: Part8.MISO, Part9.MISO, Part10.N$444
  N49: Part8.RX, Part9.RX, Part10.N$445
  N50: Part8.TX, Part9.TX, Part10.N$446
  N51: Part8.G, Part9.G, Part10.N$447
  N52: Part8.SDA, Part9.SDA, Part10.N$386
  N53: Part8.SCL, Part9.SCL, Part10.N$344
  N54: Part8.H, Part9.H, Part10.N$306
  N55: Part8.I, Part9.I, Part10.N$260
  N56: Part8.J, Part9.J, Part10.N$224
  N57: Part8.CS, Part9.K, Part10.N$209
  N58: Part8.EN, Part9.EN, Part10.N$402
  N59: Part8.VBAT, Part9.VBAT, Part10.N$408

custom parts:
  Adafruit Feather M0 Basic Proto: At the Feather M0's heart is an ATSAMD21G18 ARM Cortex M0 processor, clocked at 48 MHz and at 3.3V logic, the same one used in the new Arduino Zero. This chip has a whopping 256K of FLASH (8x more than the Atmega328 or 32u4) and 32K of RAM (16x as much)! This chip comes with built in USB so it has USB-to-Serial program & debug capability built in with no need for an FTDI-like chip. To make it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
  Adafruit FeatherWing Proto: This is the FeatherWing Proto - a prototyping add-on for all Feather boards. Using our Feather Stacking Headers or Feather Female Headers you can connect a FeatherWing on top or bottom of your Feather board and let the board take flight! This has a duplicate breakout for each pin on a Feather, as well as a bunch of plain grid proto holes. For GND and 3.3V, we give you a strip of connected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
  Adafruit FeatherWing Doubler: This is the FeatherWing Doubler - a prototyping add-on and more for all Feather boards. This is similar to our FeatherWing Proto except there are two! The magic of the Doubler comes when stacking a Feather and another board on top of the Doubler so you can work with both boards simultaneously side-by-side! The Doubler, like the Proto, has a duplicate breakout for each pin on a Feather, as well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
  Adafruit FXOS8700 + FXAS21002 9 DoF Breakout: The NXP Precision 9DoF breakout combines two of the best motion sensors we've tested here at Adafruit: The FXOS8700 3-Axis accelerometer and magnetometer, and the FXAS21002 3-axis gyroscope. These two sensors combine to make a nice 9-DoF kit, that can be used for motion and orientation sensing. In particular, we think this sensor set is ideal for AHRS-based orientation calculations: the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
  Adafruit Bluefruit LE UART Friend: The Bluefruit LE UART Friend makes it easy to add Bluetooth Low Energy connectivity to anything with a hardware or software serial port. We even have nice hardware flow control so you won't have to think about losing data. Connect to your Arduino or other microcontroller or even just a standard FTDI cable for debugging and testing.
  Adafruit Adalogger FeatherWing: This is the Adalogger FeatherWing: it adds both a battery-backed Real Time Clock and micro SD card storage to any Feather main board. This FeatherWing will make it real easy to add datalogging to any of our existing Feathers. You get both an I2C real time clock (PCF8523) with 32KHz crystal and battery backup, and a microSD socket that connects to the SPI port pins (+ extra pin for CS). Tested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
  Adafruit GPS FeatherWing: Give your Feather a sense of place, with an Ultimate GPS FeatherWing. In 2013 we designed the Ultimate GPS module to satisfy all your GPS desires - and now we have brought its power and versatility plus more to our Feather series with the Adafruit Ultimate GPS FeatherWing! This FeatherWing plugs right into your Feather board and gives it a precise, sensitive, and low power GPS module for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
